// Logisim project Carry Lookahead Adder.circ as structural Verilog: 1 circuit, main circuit main
module main (
  input  in_1,
  input  in_2,
  input  in_3,
  input  in_4,
  input  in_5,
  input  in_6,
  input  in_7,
  input  in_8,
  input  in_9,
  output out_10,
  output out_11,
  output out_12,
  output out_13,
  output out_14
);

  wire and_1_out, and_2_out, and_3_out, and_4_out, and_5_out, and_6_out, and_7_out, and_8_out, and_9_out,
       and_10_out, and_11_out, and_12_out, and_13_out, and_14_out, or_1_out, or_2_out, or_3_out, xor_1_out,
       xor_4_out, xor_5_out, xor_7_out;

  and and_1 (and_1_out, in_1, in_5);
  xor xor_1 (xor_1_out, in_1, in_5);
  xor xor_2 (out_10, in_9, xor_1_out);
  and and_2 (and_2_out, in_9, xor_1_out);
  or or_1 (or_1_out, and_2_out, and_1_out);
  xor xor_3 (out_11, or_1_out, xor_4_out);
  and and_3 (and_3_out, in_2, in_6);
  xor xor_4 (xor_4_out, in_2, in_6);
  and and_4 (and_4_out, in_9, xor_1_out, xor_4_out);
  and and_5 (and_5_out, and_1_out, xor_4_out);
  or or_2 (or_2_out, and_4_out, and_5_out, and_3_out);
  and and_6 (and_6_out, in_3, in_7);
  xor xor_5 (xor_5_out, in_3, in_7);
  xor xor_6 (out_12, or_2_out, xor_5_out);
  and and_7 (and_7_out, in_9, xor_1_out, xor_4_out, xor_5_out);
  and and_8 (and_8_out, and_1_out, xor_4_out, xor_5_out);
  and and_9 (and_9_out, and_3_out, xor_5_out);
  or or_3 (or_3_out, and_7_out, and_8_out, and_9_out, and_6_out);
  and and_10 (and_10_out, in_4, in_8);
  xor xor_7 (xor_7_out, in_4, in_8);
  xor xor_8 (out_13, or_3_out, xor_7_out);
  and and_11 (and_11_out, in_9, xor_1_out, xor_4_out, xor_5_out, xor_7_out);
  and and_12 (and_12_out, and_1_out, xor_4_out, xor_5_out, xor_7_out);
  and and_13 (and_13_out, and_3_out, xor_5_out, xor_7_out);
  and and_14 (and_14_out, and_6_out, xor_7_out);
  or or_4 (out_14, and_11_out, and_12_out, and_13_out, and_14_out, and_10_out);

  // Notes on the sheet:
  //   Generate (0)
  //   Propogate (0)
  //   Sum
  //   G(-1) (Carry (0))
  //   AND P(0)
  //   Generate (1)
  //   Propogate (1)
  //   G(-1) (Carry (0))
  //   AND P(0)
  //   AND P(1)
  //   G(0)
  //   AND P(1)
  //   Generate (2)
  //   Propogate (2)
  //   G(-1) (Carry (0))
  //   AND P(0)
  //   AND P(1)
  //   AND P(2)
  //   G(0)
  //   AND P(1)
  //   AND P(2)
  //   G(1)
  //   AND P(2)
  //   Generate (3)
  //   Propogate (3)
  //   AND P(0)
  //   AND P(1)
  //   AND P(2)
  //   G(-1) (Carry (0))
  //   AND P(3)
  //   G(0)
  //   AND P(1)
  //   AND P(2)
  //   AND P(3)
  //   G(1)
  //   AND P(2)
  //   AND P(3)
  //   G(2)
  //   AND P(3)
endmodule
