// Logisim project Full Adder.circ as structural Verilog: 1 circuit, main circuit main
module main (
  input  B,
  input  A,
  input  in_3,
  output Carry_Out,
  output SUM
);

  wire and_1_out, and_2_out, xor_2_out;

  or or_1 (Carry_Out, and_1_out, and_2_out);
  and and_1 (and_1_out, B, A);
  and and_2 (and_2_out, xor_2_out, in_3);
  xor xor_1 (SUM, xor_2_out, in_3);
  xor xor_2 (xor_2_out, A, B);

  // Notes on the sheet:
  //   AND
  //   AND
  //   XOR
  //   XOR
  //   Carry In
endmodule
