// Logisim project Ripple Carry Adder.circ as structural Verilog: 1 circuit, main circuit main
module main (
  input  A,
  input  B,
  input  A_2,
  input  B_2,
  input  A_3,
  input  B_3,
  input  A_4,
  input  B_4,
  input  Carry_In,
  output Carry_Out,
  output SUM,
  output SUM_2,
  output SUM_3,
  output SUM_4
);

  wire and_1_out, and_2_out, and_3_out, and_4_out, and_5_out, and_6_out, and_7_out, and_8_out, or_2_out,
       or_3_out, or_4_out, xor_1_out, xor_2_out, xor_3_out, xor_4_out;

  and and_1 (and_1_out, A, B);
  xor xor_1 (xor_1_out, A, B);
  and and_2 (and_2_out, A_2, B_2);
  xor xor_2 (xor_2_out, A_2, B_2);
  and and_3 (and_3_out, A_3, B_3);
  xor xor_3 (xor_3_out, A_3, B_3);
  xor xor_4 (xor_4_out, A_4, B_4);
  and and_4 (and_4_out, or_2_out, xor_1_out);
  xor xor_5 (SUM, xor_1_out, or_2_out);
  and and_5 (and_5_out, or_3_out, xor_2_out);
  xor xor_6 (SUM_2, xor_2_out, or_3_out);
  and and_6 (and_6_out, or_4_out, xor_3_out);
  and and_7 (and_7_out, A_4, B_4);
  and and_8 (and_8_out, Carry_In, xor_4_out);
  xor xor_7 (SUM_4, xor_4_out, Carry_In);
  or or_1 (Carry_Out, and_1_out, and_4_out);
  or or_2 (or_2_out, and_2_out, and_5_out);
  or or_3 (or_3_out, and_3_out, and_6_out);
  xor xor_8 (SUM_3, xor_3_out, or_4_out);
  or or_4 (or_4_out, and_7_out, and_8_out);

  // Notes on the sheet:
  //   Full Adder 4
  //   Full Adder 3
  //   Full Adder 2
  //   Full Adder 1
endmodule
