// Logisim project SR Latch.circ as structural Verilog: 1 circuit, main circuit main
module main (
  input  Set,
  input  Reset,
  output Q,
  output Q_prime
);

  nor nor_1 (Q, Set, Q_prime);
  nor nor_2 (Q_prime, Q, Reset);
endmodule
